# Fritzing sketch FabSandbox_ESP32 (saved by Fritzing 0.9.3b)
breadboards: 1

parts:
  Dev_Kit_ESP_32 = ESP32-WROOM-32D-NodeMCU
  Power_Supply_7V-12V = Power plug
  Bipolar_Stepper_Motor = Stepper Motor - Bipolar  # not connected
  DHT1 = DHT11 Humitidy and Temperature Sensor
  Push_Button = Momentary Switch [package=tactile-pth]
  R1 = Resistor [tolerance=±5% resistance=1k package="2010 [SMD]"]
  EasyDriver_V44 = EasyDriver_v44
  LDR = Photocell (LDR) [package=THT]
  R3 = Resistor [tolerance=±5% resistance=1k package="2010 [SMD]"]
  POT = Rotary Potentiometer (Small) [maximum_resistance=10kΩ package=THT]
  RELAY = KY-019 5V Relay Module [package="Breakout board"]
  LED = LED - 3mm [color="Red (633nm)" package="3 mm [THT]"]
  R5 = Resistor [tolerance=±5% resistance=220 package="0805 [SMD]"]
  SERVO_SG90 = Tower Pro SG90 servo [part_number=101246]
  RGB_(Neopixel) = SMD RGB LED (WS2812) [package=5050]  # not connected

nets:
  N1: Dev_Kit_ESP_32.SP, POT.wiper
  N2: Dev_Kit_ESP_32.SN, LDR.pin_1, R3.Pin_0
  GND: Dev_Kit_ESP_32.G34, Dev_Kit_ESP_32.CMD, DHT1.GND, Push_Button.4, EasyDriver_V44.GND, R3.Pin_1, POT.leg2, SERVO_SG90.GND
  N3: Dev_Kit_ESP_32.G33, DHT1.NULL
  N4: Dev_Kit_ESP_32.G25, EasyDriver_V44.STEP
  N5: Dev_Kit_ESP_32.G26, EasyDriver_V44.DIR
  N6: Dev_Kit_ESP_32.G27, EasyDriver_V44.ENABLE
  5V: Dev_Kit_ESP_32.5V, DHT1.VDD, R1.Pin_1, LDR.pin_0, POT.leg1, R5.Pin_0, SERVO_SG90.+5V
  N7: Dev_Kit_ESP_32.G2, LED.anode
  N8: Dev_Kit_ESP_32.G4, SERVO_SG90.Signal
  N9: Dev_Kit_ESP_32.G16, RELAY.S
  N10: Power_Supply_7V-12V.VCC, EasyDriver_V44.V+
  N11: Push_Button.3, R1.Pin_0
  N12: LED.cathode, R5.Pin_1

custom parts:
  DHT11 Humitidy and Temperature Sensor: DHT11 Humidity and Temperature Sensor
  KY-019 5V Relay Module: KY-019 5V Relay module, used to control AC circuits. (Special thanks to vanepp for fixing the PCB holes and other errors)
  Tower Pro SG90 servo: Original file by John De Cristofaro http://www.adafruit.com/products/1449 Adafruit Feedback Servo (Small) Edited by: e-radionica.com 28/9/2015
